# Fritzing sketch schematic (saved by Fritzing 1.0.2b)
breadboards: 1

parts:
  Part1 = Arduino Uno (Rev3) - ICSP
  R1 = Rotary Potentiometer (Large) [maximum_resistance=100kΩ knob_status=50% power=0.5W package=THT]
  Q1 = TRANSISTOR_NPN [package=to-92]
  D1 = Schottky Diode [part_number=1N5817 package="300 mil [THT]"]
  M1 = DC Motor [voltage_(max)=6V voltage_(min)=3V]
  R2 = Resistor [tolerance=±5% resistance=1k package="2010 [SMD]"]

nets:
  N1: Part1.A0, R1.wiper
  N2: Part1.GND, R1.leg2, Q1.E
  N3: Part1.D7, R2.Pin_0
  N4: Part1.5V, R1.leg1, D1.cathode, M1.pin_2
  N5: Q1.B, R2.Pin_1
  N6: Q1.C, D1.anode, M1.pin_1
